# Fritzing sketch CCLoader (saved by Fritzing 0.9.3b)

parts:
  Part1 = JDY-08 Bluetooth LE Module
  Part2 = Arduino Uno (Rev3)

nets:
  GND: Part1.GND, Part2.GND
  VCC: Part1.VCC, Part2.3V3
  N1: Part1.RST, Part2.D4
  N2: Part1.P21/DD, Part2.D6_PWM
  N3: Part1.P22/DC, Part2.D5_PWM

custom parts:
  JDY-08 Bluetooth LE Module: JDY-08 transparent transmission module is based on the Bluetooth 4.0 protocol standard, the working frequency of 2.4GHZ range, modulation scheme is GFSK, the maximum transmit power of 0db, maximum transmission distance of 80 meters, the use TI CC2541 chip design, allowing users to modify the device name through AT commands service UUID, transmit power, pairing password instructions, convenient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
