# Fritzing sketch Test_AT_Command (saved by Fritzing 0.9.3b)
breadboards: 1

parts:
  Part1 = JDY-08 Bluetooth LE Module
  Part2 = Arduino Uno (Rev3)
  R1 = Resistor [tolerance=±5% resistance=2.2k package=THT]
  R2 = Resistor [tolerance=±5% resistance=1k package=THT]

nets:
  GND: Part1.GND, Part2.GND, R1.Pin_0
  VCC: Part1.VCC, Part2.3V3
  N1: Part1.P16, Part2.D8
  N2: Part1.P17, R1.Pin_1, R2.Pin_0
  N3: Part2.D9_PWM, R2.Pin_1

custom parts:
  JDY-08 Bluetooth LE Module: JDY-08 transparent transmission module is based on the Bluetooth 4.0 protocol standard, the working frequency of 2.4GHZ range, modulation scheme is GFSK, the maximum transmit power of 0db, maximum transmission distance of 80 meters, the use TI CC2541 chip design, allowing users to modify the device name through AT commands service UUID, transmit power, pairing password instructions, convenient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
